# Fritzing sketch microSRCPV2 (saved by Fritzing 0.9.0b)
circuit board: 8.46667cm x 5.64444cm
breadboards: 1

parts:
  Bauteil1 = Arduino Uno (Rev3)
  IC1 = L293D [package=THT]
  M1 = DC Motor
  J1 = Basic Servo
  R1 = Rotary Potentiometer (Small) [maximum_resistance=100kΩ package=THT]
  S1 = Pushbutton [package="[THT]"]
  S2 = Pushbutton [package="[THT]"]
  S3 = Pushbutton [package="[THT]"]
  LED1 = LED - 5mm [color="Green (570nm)" package="5 mm [THT]"]
  LED2 = LED - 5mm [color="Red (633nm)" package="5 mm [THT]"]
  LED3 = LED - 5mm [color="Green (570nm)" package="5 mm [THT]"]
  LED4 = LED - 5mm [color="Red (633nm)" package="5 mm [THT]"]

nets:
  N1: Bauteil1.A0, S1.Pin_3, S1.Pin_4
  N2: Bauteil1.A1, S2.Pin_3, S2.Pin_4
  N3: Bauteil1.A2, S3.Pin_3, S3.Pin_4
  N4: Bauteil1.A3, R1.wiper
  N5: Bauteil1.D8, IC1.In_2
  N6: Bauteil1.D9_PWM, IC1.In_1
  N7: Bauteil1.D2, J1.pulse
  N8: Bauteil1.D3_PWM, IC1.Enable_1
  N9: Bauteil1.D4, LED2.anode
  N10: Bauteil1.D5_PWM, LED3.anode
  N11: Bauteil1.D6_PWM, LED4.anode
  N12: Bauteil1.D7, LED1.anode
  5V: Bauteil1.5V, IC1.+V, J1.vcc, R1.leg2
  GND: Bauteil1.GND, IC1.0V, J1.gnd, R1.leg1, S1.Pin_1, S1.Pin_2, S2.Pin_1, S2.Pin_2, S3.Pin_1, S3.Pin_2, LED1.cathode, LED2.cathode, LED3.cathode, LED4.cathode
  N13: Bauteil1.VIN, IC1.+Vmotor
  N14: IC1.Out_1_(_Controlled_by_Enable_1_), M1.pin_2
  N15: IC1.Out_2_(_Controlled_by_Enable_1_), M1.pin_1
